// Logisim project ciulpan_andrei_872394_arch1lab_progetto.circ as structural Verilog: 6 circuits, main circuit main
module main (
);

  wire _1, _2, _3, _4, and_1_out, and_2_out, CK, L, not_1_out, not_2_out, not_3_out, not_4_out, not_5_out,
       ON_OFF_out, or_1_out, or_2_out, PWR, R, score_1_in_progress, W;
  wire [1:0] SEL;
  wire [3:0] H1, H2, M, message_display_1_out_2, message_display_1_out_3, message_display_1_out_4,
       message_display_1_out_5, message_display_1_out_6, message_display_1_out_7, message_display_1_out_8,
       message_display_1_out_9, message_display_1_out_10, message_display_1_out_11, message_display_1_out_12,
       message_display_1_out_13, message_display_1_out_14, message_display_1_out_15,
       message_display_1_out_16, message_display_1_out_17, message_display_1_out_18,
       message_display_1_out_19, message_display_1_out_20, message_display_1_out_21,
       message_display_1_out_22, message_display_1_out_23, message_display_1_out_24,
       message_display_1_out_25, message_display_1_out_26, message_display_1_out_27,
       message_display_1_out_28, message_display_1_out_29, message_display_1_out_30,
       message_display_1_out_31, random_tile_generator_1_pseudo_random_bit_sequence, ROW0,
       shift_register_1_q0, shift_register_1_q1, shift_register_1_q2, shift_register_1_q3,
       shift_register_1_q4, shift_register_1_q5, shift_register_1_q6;
  wire [7:0] tile_doubler_1_out_9, tile_doubler_1_out_10, tile_doubler_1_out_11, tile_doubler_1_out_12,
       tile_doubler_1_out_13, tile_doubler_1_out_14, tile_doubler_1_out_15, tile_doubler_1_out_16;

  and and_1 (and_1_out, score_1_in_progress, PWR);
  not not_1 (not_1_out, PWR);
  Score score_1 (
    .ROW0(ROW0), .HITS__LSD(H1), .Misses(M), .B1(_1), .B2(_2), .R(or_1_out), .B3(_3), .B4(_4),
    .HITS__MSD(H2), .WIN__20_pts(W), .LOSE__9_misses(L), .IN_PROGRESS(score_1_in_progress));
  or or_1 (or_1_out, R, not_2_out);
  not not_2 (not_2_out, PWR);
  Priority_Encoder #(.select(2)) priority_encoder_1 (
    .in0(and_1_out), .in1(W), .in2(L), .in3(not_1_out), .out(SEL));  // open: gs, en_out, en_in
  not not_3 (not_3_out, W);
  not not_4 (not_4_out, L);
  or or_2 (or_2_out, L, R, not_5_out);
  and and_2 (and_2_out, not_3_out, not_4_out);
  Random_Tile_Generator random_tile_generator_1 (
    .ON(PWR), .Pseudo_Random_Bit_Sequence(random_tile_generator_1_pseudo_random_bit_sequence));
  Shift_Register #(.width(4)) shift_register_1 (
    .shift(and_2_out), .in(random_tile_generator_1_pseudo_random_bit_sequence), .clk(CK), .clr(or_2_out),
    .q0(shift_register_1_q0), .q1(shift_register_1_q1), .q2(shift_register_1_q2), .q3(shift_register_1_q3),
    .q4(shift_register_1_q4), .q5(shift_register_1_q5), .q6(shift_register_1_q6), .q7(ROW0));  // open: out, load, d0, d1, d2, d3, d4, d5, d6, d7
  not not_5 (not_5_out, PWR);
  DotMatrix #(.inputtype("row"), .matrixcols(8), .matrixrows(8)) dotmatrix_1 (
    .row0(tile_doubler_1_out_9), .row1(tile_doubler_1_out_10), .row2(tile_doubler_1_out_11),
    .row3(tile_doubler_1_out_12), .row4(tile_doubler_1_out_13), .row5(tile_doubler_1_out_14),
    .row6(tile_doubler_1_out_15), .row7(tile_doubler_1_out_16));
  Tile_doubler tile_doubler_1 (
    .in_1(shift_register_1_q0), .in_2(shift_register_1_q1), .in_3(shift_register_1_q2),
    .in_4(shift_register_1_q3), .in_5(shift_register_1_q4), .in_6(shift_register_1_q5),
    .in_7(shift_register_1_q6), .in_8(ROW0), .out_9(tile_doubler_1_out_9), .out_10(tile_doubler_1_out_10),
    .out_11(tile_doubler_1_out_11), .out_12(tile_doubler_1_out_12), .out_13(tile_doubler_1_out_13),
    .out_14(tile_doubler_1_out_14), .out_15(tile_doubler_1_out_15), .out_16(tile_doubler_1_out_16));
  DotMatrix #(.matrixcols(30), .matrixrows(4)) dotmatrix_2 (
    .col0(message_display_1_out_31), .col1(message_display_1_out_30), .col2(message_display_1_out_29),
    .col3(message_display_1_out_28), .col4(message_display_1_out_27), .col5(message_display_1_out_26),
    .col6(message_display_1_out_25), .col7(message_display_1_out_24), .col8(message_display_1_out_23),
    .col9(message_display_1_out_22), .col10(message_display_1_out_21), .col11(message_display_1_out_20),
    .col12(message_display_1_out_19), .col13(message_display_1_out_18), .col14(message_display_1_out_17),
    .col15(message_display_1_out_16), .col16(message_display_1_out_15), .col17(message_display_1_out_14),
    .col18(message_display_1_out_13), .col19(message_display_1_out_12), .col20(message_display_1_out_11),
    .col21(message_display_1_out_10), .col22(message_display_1_out_9), .col23(message_display_1_out_8),
    .col24(message_display_1_out_7), .col25(message_display_1_out_6), .col26(message_display_1_out_5),
    .col27(message_display_1_out_4), .col28(message_display_1_out_3), .col29(message_display_1_out_2));
  Button u__2 (.out(_2));
  Button u__1 (.out(_1));
  Button u__4 (.out(_4));
  Button u__3 (.out(_3));
  Hex_Digit_Display hex_digit_display_1 (.value(H2));  // open: dp
  Hex_Digit_Display hex_digit_display_2 (.value(H1));  // open: dp
  Hex_Digit_Display hex_digit_display_3 (.value(M));  // open: dp
  Message_Display message_display_1 (
    .out_2(message_display_1_out_2), .SEL(SEL), .out_3(message_display_1_out_3),
    .out_4(message_display_1_out_4), .out_5(message_display_1_out_5), .out_6(message_display_1_out_6),
    .out_7(message_display_1_out_7), .out_8(message_display_1_out_8), .out_9(message_display_1_out_9),
    .out_10(message_display_1_out_10), .out_11(message_display_1_out_11), .out_12(message_display_1_out_12),
    .out_13(message_display_1_out_13), .out_14(message_display_1_out_14), .out_15(message_display_1_out_15),
    .out_16(message_display_1_out_16), .out_17(message_display_1_out_17), .out_18(message_display_1_out_18),
    .out_19(message_display_1_out_19), .out_20(message_display_1_out_20), .out_21(message_display_1_out_21),
    .out_22(message_display_1_out_22), .out_23(message_display_1_out_23), .out_24(message_display_1_out_24),
    .out_25(message_display_1_out_25), .out_26(message_display_1_out_26), .out_27(message_display_1_out_27),
    .out_28(message_display_1_out_28), .out_29(message_display_1_out_29), .out_30(message_display_1_out_30),
    .out_31(message_display_1_out_31));
  Clock clock_1 (.out(CK));
  LED led_1 (.in(PWR));
  ON___OFF_Button on_off_button_1 (.in_1(ON_OFF_out), .out_2(PWR));
  Button ON_OFF (.out(ON_OFF_out));
  Button RESET (.out(R));

  // Notes on the sheet:
  //   HITS
  //   MISSES (max 9)
endmodule

module Score (
  input  [3:0] ROW0,
  input  B1,
  input  B2,
  input  B3,
  input  B4,
  input  R,
  output [3:0] HITS__LSD,
  output [3:0] HITS__MSD,
  output WIN__20_pts,
  output IN_PROGRESS,
  output [3:0] Misses,
  output LOSE__9_misses
);

  wire and_1_out, and_2_out, and_3_out, and_4_out, and_5_out, clock_1_out, clock_2_out, comparator_1_eq,
       comparator_2_eq, counter_2_carry, not_1_out, not_2_out, not_3_out, not_4_out, not_5_out, not_6_out,
       not_7_out, not_8_out, not_9_out, not_10_out, or_1_out, or_2_out, or_3_out, or_4_out, or_5_out,
       or_6_out, or_7_out, or_8_out;

  not not_1 (not_1_out, B1);
  not not_2 (not_2_out, ROW0[3]);
  not not_3 (not_3_out, B2);
  not not_4 (not_4_out, ROW0[2]);
  not not_5 (not_5_out, B3);
  not not_6 (not_6_out, ROW0[1]);
  not not_7 (not_7_out, B4);
  not not_8 (not_8_out, ROW0[0]);
  and and_1 (and_1_out, B1, ROW0[3]);
  and and_2 (and_2_out, B2, ROW0[2]);
  and and_3 (and_3_out, B3, ROW0[1]);
  and and_4 (and_4_out, B4, ROW0[0]);
  or or_1 (or_1_out, B1, B2, B3, B4, ROW0[3], ROW0[2], ROW0[1], ROW0[0]);
  or or_2 (or_2_out, not_1_out, B2, B3, B4, not_2_out, ROW0[2], ROW0[1], ROW0[0]);
  or or_3 (or_3_out, B1, not_3_out, B3, B4, ROW0[3], not_4_out, ROW0[1], ROW0[0]);
  or or_4 (or_4_out, B1, B2, not_5_out, B4, ROW0[3], ROW0[2], not_6_out, ROW0[0]);
  or or_5 (or_5_out, B1, B2, B3, not_7_out, ROW0[3], ROW0[2], ROW0[1], not_8_out);
  or or_6 (or_6_out, and_1_out, and_2_out, and_3_out, and_4_out);
  Clock clock_1 (.out(clock_1_out));
  and and_5 (and_5_out, or_1_out, or_2_out, or_3_out, or_4_out, or_5_out);
  Counter #(.width(4), .max('h2), .ongoal("stay"), .trigger("falling")) counter_1 (
    .Q(HITS__MSD), .clk(counter_2_carry), .clr(or_7_out));  // open: load, D, count, carry
  Counter #(.width(4), .max('h9), .trigger("falling")) counter_2 (
    .count(or_6_out), .Q(HITS__LSD), .carry(counter_2_carry), .clk(clock_1_out), .clr(or_7_out));  // open: load, D
  or or_7 (or_7_out, LOSE__9_misses, R);
  not not_9 (not_9_out, LOSE__9_misses);
  and and_6 (IN_PROGRESS, not_9_out, not_10_out);
  not not_10 (not_10_out, WIN__20_pts);
  Counter #(.width(4), .max('h9), .ongoal("stay"), .trigger("falling")) counter_3 (
    .count(and_5_out), .Q(Misses), .carry(LOSE__9_misses), .clk(clock_2_out), .clr(or_8_out));  // open: load, D
  or or_8 (or_8_out, R, WIN__20_pts);
  Clock clock_2 (.out(clock_2_out));
  Comparator #(.width(4)) comparator_1 (.a(HITS__LSD), .b(4'b0000), .eq(comparator_1_eq));  // open: gt, lt
  Comparator #(.width(4)) comparator_2 (.a(HITS__MSD), .b(4'b0010), .eq(comparator_2_eq));  // open: gt, lt
  and and_7 (WIN__20_pts, comparator_1_eq, comparator_2_eq);

  // Other names for the same wires on the sheet: L = LOSE__9_misses; W = WIN__20_pts
endmodule

// Tile
module Random_Tile_Generator (
  input  ON,
  output [3:0] Pseudo_Random_Bit_Sequence
);

  wire and_1_out, and_2_out, and_3_out, and_4_out, and_5_out, and_6_out, and_7_out, and_8_out, CLK_out,
       not_1_out, not_2_out, not_3_out, not_4_out, not_5_out, not_6_out, not_7_out, not_8_out, not_9_out,
       not_10_out, not_11_out, not_12_out, not_13_out, not_14_out, not_15_out, not_16_out, not_17_out,
       not_18_out;
  wire [3:0] random_1_out;

  Clock CLK (.out(CLK_out));
  Random #(.width(4)) random_1 (.clk(CLK_out), .next(ON), .out(random_1_out));  // open: clr
  not not_1 (not_1_out, random_1_out[1]);
  and and_1 (and_1_out, random_1_out[0], not_1_out, not_2_out, not_3_out);
  not not_2 (not_2_out, random_1_out[2]);
  not not_3 (not_3_out, random_1_out[3]);
  not not_4 (not_4_out, random_1_out[1]);
  and and_2 (and_2_out, random_1_out[0], not_4_out, not_5_out, random_1_out[3]);
  not not_5 (not_5_out, random_1_out[2]);
  not not_6 (not_6_out, random_1_out[0]);
  and and_3 (and_3_out, not_6_out, random_1_out[1], not_7_out, not_8_out);
  not not_7 (not_7_out, random_1_out[2]);
  not not_8 (not_8_out, random_1_out[3]);
  not not_9 (not_9_out, random_1_out[0]);
  and and_4 (and_4_out, not_9_out, random_1_out[1], not_10_out, random_1_out[3]);
  not not_10 (not_10_out, random_1_out[2]);
  not not_11 (not_11_out, random_1_out[0]);
  not not_12 (not_12_out, random_1_out[1]);
  and and_5 (and_5_out, not_11_out, not_12_out, random_1_out[2], not_13_out);
  not not_13 (not_13_out, random_1_out[3]);
  not not_14 (not_14_out, random_1_out[1]);
  and and_6 (and_6_out, random_1_out[0], not_14_out, random_1_out[2], random_1_out[3]);
  not not_15 (not_15_out, random_1_out[0]);
  not not_16 (not_16_out, random_1_out[1]);
  and and_7 (and_7_out, not_15_out, not_16_out, not_17_out, random_1_out[3]);
  not not_17 (not_17_out, random_1_out[2]);
  not not_18 (not_18_out, random_1_out[0]);
  and and_8 (and_8_out, not_18_out, random_1_out[1], random_1_out[2], random_1_out[3]);
  or or_1 (Pseudo_Random_Bit_Sequence[0], and_1_out, and_2_out);
  or or_2 (Pseudo_Random_Bit_Sequence[1], and_3_out, and_4_out);
  or or_3 (Pseudo_Random_Bit_Sequence[2], and_5_out, and_6_out);
  or or_4 (Pseudo_Random_Bit_Sequence[3], and_7_out, and_8_out);
endmodule

// PWR
module ON___OFF_Button (
  input  in_1,
  output out_2
);

  wire clock_1_out;

  Counter #(.width(1), .max('h1)) counter_1 (.count(in_1), .Q(out_2), .clk(clock_1_out));  // open: load, D, carry, clr
  Clock clock_1 (.out(clock_1_out));
endmodule

// DISPLAY
module Message_Display (
  input  [1:0] SEL,
  output [3:0] out_2,
  output [3:0] out_3,
  output [3:0] out_4,
  output [3:0] out_5,
  output [3:0] out_6,
  output [3:0] out_7,
  output [3:0] out_8,
  output [3:0] out_9,
  output [3:0] out_10,
  output [3:0] out_11,
  output [3:0] out_12,
  output [3:0] out_13,
  output [3:0] out_14,
  output [3:0] out_15,
  output [3:0] out_16,
  output [3:0] out_17,
  output [3:0] out_18,
  output [3:0] out_19,
  output [3:0] out_20,
  output [3:0] out_21,
  output [3:0] out_22,
  output [3:0] out_23,
  output [3:0] out_24,
  output [3:0] out_25,
  output [3:0] out_26,
  output [3:0] out_27,
  output [3:0] out_28,
  output [3:0] out_29,
  output [3:0] out_30,
  output [3:0] out_31
);

  Multiplexer #(.select(2), .width(4)) multiplexer_1 (
    .in0(4'b0000), .in1(4'b0000), .in2(4'b1000), .in3(4'b0000), .out(out_2), .sel(SEL));  // open: en
  Multiplexer #(.select(2), .width(4)) multiplexer_2 (
    .in0(4'b1100), .in1(4'b1111), .in2(4'b1111), .in3(4'b0000), .out(out_12), .sel(SEL));  // open: en
  Multiplexer #(.select(2), .width(4)) multiplexer_3 (
    .in0(4'b1110), .in1(4'b0000), .in2(4'b0000), .in3(4'b0000), .out(out_22), .sel(SEL));  // open: en
  Multiplexer #(.select(2), .width(4)) multiplexer_4 (
    .in0(4'b0000), .in1(4'b1111), .in2(4'b1111), .in3(4'b0000), .out(out_3), .sel(SEL));  // open: en
  Multiplexer #(.select(2), .width(4)) multiplexer_5 (
    .in0(4'b0000), .in1(4'b0001), .in2(4'b0000), .in3(4'b0000), .out(out_13), .sel(SEL));  // open: en
  Multiplexer #(.select(2), .width(4)) multiplexer_6 (
    .in0(4'b1010), .in1(4'b1111), .in2(4'b1111), .in3(4'b0000), .out(out_23), .sel(SEL));  // open: en
  Multiplexer #(.select(2), .width(4)) multiplexer_7 (
    .in0(4'b0000), .in1(4'b0010), .in2(4'b1000), .in3(4'b0000), .out(out_4), .sel(SEL));  // open: en
  Multiplexer #(.select(2), .width(4)) multiplexer_8 (
    .in0(4'b1111), .in1(4'b0010), .in2(4'b0001), .in3(4'b0000), .out(out_14), .sel(SEL));  // open: en
  Multiplexer #(.select(2), .width(4)) multiplexer_9 (
    .in0(4'b1111), .in1(4'b1001), .in2(4'b1001), .in3(4'b0000), .out(out_24), .sel(SEL));  // open: en
  Multiplexer #(.select(2), .width(4)) multiplexer_10 (
    .in0(4'b0000), .in1(4'b0100), .in2(4'b0000), .in3(4'b0000), .out(out_5), .sel(SEL));  // open: en
  Multiplexer #(.select(2), .width(4)) multiplexer_11 (
    .in0(4'b1010), .in1(4'b0001), .in2(4'b0001), .in3(4'b0000), .out(out_15), .sel(SEL));  // open: en
  Multiplexer #(.select(2), .width(4)) multiplexer_12 (
    .in0(4'b0000), .in1(4'b1111), .in2(4'b1111), .in3(4'b0000), .out(out_25), .sel(SEL));  // open: en
  Multiplexer #(.select(2), .width(4)) multiplexer_13 (
    .in0(4'b0000), .in1(4'b1111), .in2(4'b1000), .in3(4'b0000), .out(out_6), .sel(SEL));  // open: en
  Multiplexer #(.select(2), .width(4)) multiplexer_14 (
    .in0(4'b1111), .in1(4'b1111), .in2(4'b1111), .in3(4'b0000), .out(out_16), .sel(SEL));  // open: en
  Multiplexer #(.select(2), .width(4)) multiplexer_15 (
    .in0(4'b0000), .in1(4'b0000), .in2(4'b0000), .in3(4'b0000), .out(out_26), .sel(SEL));  // open: en
  Multiplexer #(.select(2), .width(4)) multiplexer_16 (
    .in0(4'b0000), .in1(4'b0000), .in2(4'b1111), .in3(4'b0000), .out(out_7), .sel(SEL));  // open: en
  Multiplexer #(.select(2), .width(4)) multiplexer_17 (
    .in0(4'b0000), .in1(4'b0000), .in2(4'b0000), .in3(4'b0000), .out(out_17), .sel(SEL));  // open: en
  Multiplexer #(.select(2), .width(4)) multiplexer_18 (
    .in0(4'b0000), .in1(4'b1100), .in2(4'b1100), .in3(4'b0000), .out(out_27), .sel(SEL));  // open: en
  Multiplexer #(.select(2), .width(4)) multiplexer_19 (
    .in0(4'b1100), .in1(4'b1111), .in2(4'b0001), .in3(4'b0000), .out(out_8), .sel(SEL));  // open: en
  Multiplexer #(.select(2), .width(4)) multiplexer_20 (
    .in0(4'b0001), .in1(4'b0000), .in2(4'b0000), .in3(4'b0000), .out(out_18), .sel(SEL));  // open: en
  Multiplexer #(.select(2), .width(4)) multiplexer_21 (
    .in0(4'b0000), .in1(4'b0100), .in2(4'b0100), .in3(4'b0000), .out(out_28), .sel(SEL));  // open: en
  Multiplexer #(.select(2), .width(4)) multiplexer_22 (
    .in0(4'b0100), .in1(4'b1001), .in2(4'b0000), .in3(4'b0000), .out(out_9), .sel(SEL));  // open: en
  Multiplexer #(.select(2), .width(4)) multiplexer_23 (
    .in0(4'b0001), .in1(4'b1111), .in2(4'b1111), .in3(4'b0000), .out(out_19), .sel(SEL));  // open: en
  Multiplexer #(.select(2), .width(4)) multiplexer_24 (
    .in0(4'b0000), .in1(4'b0111), .in2(4'b0111), .in3(4'b0000), .out(out_29), .sel(SEL));  // open: en
  Multiplexer #(.select(2), .width(4)) multiplexer_25 (
    .in0(4'b0111), .in1(4'b1111), .in2(4'b1111), .in3(4'b0000), .out(out_10), .sel(SEL));  // open: en
  Multiplexer #(.select(2), .width(4)) multiplexer_26 (
    .in0(4'b1111), .in1(4'b0001), .in2(4'b0001), .in3(4'b0000), .out(out_20), .sel(SEL));  // open: en
  Multiplexer #(.select(2), .width(4)) multiplexer_27 (
    .in0(4'b0000), .in1(4'b0100), .in2(4'b0100), .in3(4'b0000), .out(out_30), .sel(SEL));  // open: en
  Multiplexer #(.select(2), .width(4)) multiplexer_28 (
    .in0(4'b0100), .in1(4'b0000), .in2(4'b1001), .in3(4'b0000), .out(out_11), .sel(SEL));  // open: en
  Multiplexer #(.select(2), .width(4)) multiplexer_29 (
    .in0(4'b0000), .in1(4'b1111), .in2(4'b1111), .in3(4'b0000), .out(out_21), .sel(SEL));  // open: en
  Multiplexer #(.select(2), .width(4)) multiplexer_30 (
    .in0(4'b0000), .in1(4'b1100), .in2(4'b1100), .in3(4'b0000), .out(out_31), .sel(SEL));  // open: en

  // Notes on the sheet:
  //   21-30
  //   11-20
  //   1-10
endmodule

// 2x tiles
module Tile_doubler (
  input  [3:0] in_1,
  input  [3:0] in_2,
  input  [3:0] in_3,
  input  [3:0] in_4,
  input  [3:0] in_5,
  input  [3:0] in_6,
  input  [3:0] in_7,
  input  [3:0] in_8,
  output [7:0] out_9,
  output [7:0] out_10,
  output [7:0] out_11,
  output [7:0] out_12,
  output [7:0] out_13,
  output [7:0] out_14,
  output [7:0] out_15,
  output [7:0] out_16
);


  assign out_9 = {{2{in_1[3]}}, {2{in_1[2]}}, {2{in_1[1]}}, {2{in_1[0]}}};
  assign out_10 = {{2{in_2[3]}}, {2{in_2[2]}}, {2{in_2[1]}}, {2{in_2[0]}}};
  assign out_11 = {{2{in_3[3]}}, {2{in_3[2]}}, {2{in_3[1]}}, {2{in_3[0]}}};
  assign out_12 = {{2{in_4[3]}}, {2{in_4[2]}}, {2{in_4[1]}}, {2{in_4[0]}}};
  assign out_13 = {{2{in_5[3]}}, {2{in_5[2]}}, {2{in_5[1]}}, {2{in_5[0]}}};
  assign out_14 = {{2{in_6[3]}}, {2{in_6[2]}}, {2{in_6[1]}}, {2{in_6[0]}}};
  assign out_15 = {{2{in_7[3]}}, {2{in_7[2]}}, {2{in_7[1]}}, {2{in_7[0]}}};
  assign out_16 = {{2{in_8[3]}}, {2{in_8[2]}}, {2{in_8[1]}}, {2{in_8[0]}}};
endmodule
